# Fritzing sketch control (saved by Fritzing 0.9.3b)
circuit board: 11.9936cm x 4.8879cm
circuit board: 4.91421cm x 5.45358cm

parts:
  7-Segment1 = 7 Segment Display
  7-Segment2 = 7 Segment Display
  R9 = Resistor [tolerance=±5% resistance=220 package=THT]
  R16 = Resistor [tolerance=±5% resistance=220 package=THT]
  R15 = Resistor [tolerance=±5% resistance=220 package=THT]
  R14 = Resistor [tolerance=±5% resistance=220 package=THT]
  R10 = Resistor [tolerance=±5% resistance=220 package=THT]
  R11 = Resistor [tolerance=±5% resistance=220 package=THT]
  R12 = Resistor [tolerance=±5% resistance=220 package=THT]
  R17 = Resistor [tolerance=±5% resistance=220 package=THT]
  R3 = Resistor [tolerance=±5% resistance=220 package=THT]
  R7 = Resistor [tolerance=±5% resistance=220 package=THT]
  R8 = Resistor [tolerance=±5% resistance=220 package=THT]
  R4 = Resistor [tolerance=±5% resistance=220 package=THT]
  R5 = Resistor [tolerance=±5% resistance=220 package=THT]
  R2 = Resistor [tolerance=±5% resistance=220 package=THT]
  R6 = Resistor [tolerance=±5% resistance=220 package=THT]
  U2 = 74HC595 [package="DIP16 [THT]"]
  U1 = 74HC595 [package="DIP16 [THT]"]
  R1 = Resistor [tolerance=±5% resistance=220 package=THT]
  J4(DC_5_5) = Power Jack [package=power_jack_slot]
  J1 = shrouded pin header, 6 pins [form="♂ (shrouded male)"]
  J5 = female pin header, 2 pins [form="♀ (female)"]
  J3 = shrouded pin header, 6 pins [form="♂ (shrouded male)"]
  J2 = shrouded pin header, 8 pins [form="♂ (shrouded male)"]
  L293D = L293D [package=THT]

nets:
  N1: 7-Segment1.Segment_G, R4.Pin_1
  N2: 7-Segment1.Segment_F, R3.Pin_1
  GND: 7-Segment1.common_anode, 7-Segment2.common_anode, U2.GND, U2.OE, U1.GND, U1.OE, J1.pin1
  N3: 7-Segment1.Segment_E, R2.Pin_1
  N4: 7-Segment1.Segment_D, R1.Pin_1
  N5: 7-Segment1.Segment_DP, R5.Pin_0
  N6: 7-Segment1.Segment_C, R6.Pin_0
  N7: 7-Segment1.Segment_B, R7.Pin_0
  N8: 7-Segment1.Segment_A, R8.Pin_0
  N9: 7-Segment2.Segment_G, R12.Pin_1
  N10: 7-Segment2.Segment_F, R11.Pin_1
  N11: 7-Segment2.Segment_E, R10.Pin_1
  N12: 7-Segment2.Segment_D, R9.Pin_1
  N13: 7-Segment2.Segment_DP, R14.Pin_0
  N14: 7-Segment2.Segment_C, R15.Pin_0
  N15: 7-Segment2.Segment_B, R16.Pin_0
  N16: 7-Segment2.Segment_A, R17.Pin_0
  N17: R9.Pin_0, U2.Q0
  N18: R16.Pin_1, U2.Q5
  N19: R15.Pin_1, U2.Q6
  N20: R14.Pin_1, U2.Q7
  N21: R10.Pin_0, U2.Q1
  N22: R11.Pin_0, U2.Q2
  N23: R12.Pin_0, U2.Q3
  N24: R17.Pin_1, U2.Q4
  N25: R3.Pin_0, U1.Q2
  N26: R7.Pin_1, U1.Q5
  N27: R8.Pin_1, U1.Q4
  N28: R4.Pin_0, U1.Q3
  N29: R5.Pin_1, U1.Q7
  N30: R2.Pin_0, U1.Q1
  N31: R6.Pin_1, U1.Q6
  VCC: U2.MR, U2.VCC, U1.MR, U1.VCC, J1.pin5
  N32: U2.SH_CP, U1.SH_CP, J1.pin3
  N33: U2.ST_CP, U1.ST_CP, J1.pin4
  N34: U2.DS, U1.Q7'
  N35: U1.DS, J1.pin2
  N36: U1.Q0, R1.Pin_0
  N37: J4(DC_5_5).GNDBREAK, J4(DC_5_5).GND, J5.pin1, L293D.0V
  N38: J4(DC_5_5).PWR, L293D.+Vmotor
  N39: J5.pin2, L293D.Out_1_(_Controlled_by_Enable_1_)
  N40: J3.pin1, J2.pin1
  N41: J3.pin2, J2.pin2
  N42: J3.pin3, J2.pin3
  N43: J3.pin4, J2.pin6
  N44: J3.pin5, J2.pin7
  N45: J2.pin4, L293D.In_1
  N46: J2.pin5, L293D.Enable_1

notes:
  @Qinka
  vObj805-vis-m
  https://github.com
  Obj805
  /Qinka/Obj805
  display-p
  motor-p
